# Fritzing sketch project (saved by Fritzing 1.0.6)
breadboards: 1

parts:
  LCD1 = LCD screen
  Part1 = Arduino Uno (Rev3) - ICSP
  Part3 = Thumb Joystick  # not connected
  S1 = Pushbutton [package="[THT]"]
  S2 = Pushbutton [package="[THT]"]
  S3 = Pushbutton [package="[THT]"]  # not connected
  LCD2 = 1_54in tft lcd  # not connected
  Part4 = Thumb Joystick  # not connected
  R1 = Resistor [tolerance=±5% power=0.25W resistance=10k package=THT]
  R2 = Resistor [tolerance=±5% power=0.25W resistance=10k package=THT]
  R3 = TRIMPOT [maximum_resistance=10kΩ knob_status=50% power=0.5W package=trimpot-3mm-2]

nets:
  VSS: LCD1.VSS, LCD1.V0, Part1.GND, R1.Pin_1, R2.Pin_1, R3.CCW, R3.WIPER, R3.CW
  VDD: LCD1.VDD, Part1.5V, S1.Pin_3, S1.Pin_4, S2.Pin_3, S2.Pin_4
  N1: Part1.D2, S1.Pin_1, S1.Pin_2, R1.Pin_0
  N2: Part1.D4, S2.Pin_1, S2.Pin_2, R2.Pin_0

custom parts:
  1_54in tft lcd: This is the DONGKER 1.54'' LCD Display Module, SPI 240x240 1.54'' LCD Display Module ST7789 Driver 240x240 3.3V IPS LCD Display Screen Module. The 1.54" display has 240x240 color pixels.
